// Logisim project Booths_multiplication.circ as structural Verilog: 12 circuits, main circuit Booths_multiplier
module Booths_multiplier (
  input  [3:0] M_input,
  input  [3:0] Q_input,
  input  Reset
);

  wire clock_1_out, controller_1_c0, controller_1_c1, controller_1_cl_a_qm1, controller_1_dec_cnt,
       controller_1_load_a, controller_1_load_m_q_cnt, controller_1_shr, shift_register_1_out,
       shift_register_3_out, shift_register_3_q3, shift_register_4_q0;
  wire [2:0] counter_1_q;
  wire [3:0] alu_4_bit_1_result, shift_register_1_q3, shift_register_2_q3;

  Clock clock_1 (.out(clock_1_out));
  Controller controller_1 (
    .Clk(clock_1_out), .Reset(Reset), .Q0(shift_register_3_q3), .Qm1(shift_register_4_q0),
    .Count(counter_1_q), .Cl_A_Qm1(controller_1_cl_a_qm1), .LOad_M_Q_Cnt(controller_1_load_m_q_cnt),
    .Load_A(controller_1_load_a), .C0(controller_1_c0), .C1(controller_1_c1), .Shr(controller_1_shr),
    .Dec_Cnt(controller_1_dec_cnt));
  Counter #(.max('h4), .width(3)) counter_1 (
    .load(controller_1_load_m_q_cnt), .D(3'b100), .count(controller_1_dec_cnt), .Q(counter_1_q), .up(1'b0),
    .clk(clock_1_out));  // open: carry, clr
  Shift_Register #(.length(4)) shift_register_1 (
    .shift(controller_1_shr), .in(shift_register_1_q3[3]), .clk(clock_1_out), .out(shift_register_1_out),
    .load(controller_1_load_a), .clr(controller_1_cl_a_qm1), .d0(alu_4_bit_1_result[3]),
    .q0(shift_register_1_q3[3]), .d1(alu_4_bit_1_result[2]), .q1(shift_register_1_q3[2]),
    .d2(alu_4_bit_1_result[1]), .q2(shift_register_1_q3[1]), .d3(alu_4_bit_1_result[0]),
    .q3(shift_register_1_q3[0]));
  Shift_Register #(.length(4)) shift_register_2 (
    .shift(1'b0), .clk(clock_1_out), .load(controller_1_load_m_q_cnt), .d0(M_input[3]),
    .q0(shift_register_2_q3[3]), .d1(M_input[2]), .q1(shift_register_2_q3[2]), .d2(M_input[1]),
    .q2(shift_register_2_q3[1]), .d3(M_input[0]), .q3(shift_register_2_q3[0]));  // open: in, out, clr
  ALU_4_bit alu_4_bit_1 (
    .A(shift_register_1_q3), .B(shift_register_2_q3), .Control0(controller_1_c0), .Control1(controller_1_c1),
    .Result(alu_4_bit_1_result));  // open: Zero, Negative, Overflow, Carry
  Shift_Register #(.length(4)) shift_register_3 (
    .shift(controller_1_shr), .in(shift_register_1_out), .clk(clock_1_out), .out(shift_register_3_out),
    .load(controller_1_load_m_q_cnt), .d0(Q_input[3]), .d1(Q_input[2]), .d2(Q_input[1]), .d3(Q_input[0]),
    .q3(shift_register_3_q3));  // open: clr, q0, q1, q2
  Shift_Register #(.length(1)) shift_register_4 (
    .shift(controller_1_shr), .in(shift_register_3_out), .clk(clock_1_out), .clr(controller_1_cl_a_qm1),
    .q0(shift_register_4_q0));  // open: out, load, d0

  // Notes on the sheet:
  //   M
  //   A
  //   Q
  //   Q -1
endmodule

// 4-bit AND
module and_4_bit (
  input  [3:0] A,
  input  [3:0] B,
  output [3:0] Result
);

  assign Result = A & B;  // AND_Gate and_1, 4 bits wide
endmodule

// 4-bit OR
module OR_4_bit (
  input  [3:0] A,
  input  [3:0] B,
  output [3:0] Result
);

  assign Result = A | B;  // OR_Gate or_1, 4 bits wide
endmodule

module Full_adder (
  input  Carry_in,
  input  A,
  input  B,
  output Result,
  output Carry_out
);

  wire and_1_out, and_2_out, xor_1_out;

  and and_1 (and_1_out, B, A);
  xor xor_1 (xor_1_out, A, B);
  or or_1 (Carry_out, and_1_out, and_2_out);
  and and_2 (and_2_out, xor_1_out, Carry_in);
  xor xor_2 (Result, Carry_in, xor_1_out);
endmodule

module full_adder_4_bit (
  input  Carry_in,
  input  [3:0] A,
  input  [3:0] B,
  output [3:0] Result,
  output Carry
);

  wire full_adder_1_carry_out, full_adder_2_carry_out, full_adder_3_carry_out;

  Full_adder full_adder_1 (
    .A(A[0]), .B(B[0]), .Carry_in(Carry_in), .Carry_out(full_adder_1_carry_out), .Result(Result[0]));
  Full_adder full_adder_2 (
    .A(A[1]), .B(B[1]), .Carry_in(full_adder_1_carry_out), .Carry_out(full_adder_2_carry_out),
    .Result(Result[1]));
  Full_adder full_adder_3 (
    .A(A[2]), .B(B[2]), .Carry_in(full_adder_2_carry_out), .Carry_out(full_adder_3_carry_out),
    .Result(Result[2]));
  Full_adder full_adder_4 (
    .A(A[3]), .B(B[3]), .Carry_in(full_adder_3_carry_out), .Carry_out(Carry), .Result(Result[3]));
endmodule

module xor_4_bit (
  input  Control,
  input  [3:0] B,
  output [3:0] Result
);

  wire [3:0] bit_extender_1_out;

  assign bit_extender_1_out = {{3{Control}}, Control};  // Bit_Extender bit_extender_1
  assign Result = bit_extender_1_out ^ B;  // XOR_Gate xor_1, 4 bits wide
endmodule

// 32-bit \nADD/SUB
module Add_sub (
  input  Sub,
  input  [3:0] A,
  input  [3:0] B,
  output [3:0] Result,
  output Carry,
  output Overflow
);

  wire and_1_out, and_2_out, not_1_out, not_2_out, not_3_out, sign_bit_out_1_ms_bit, sign_bit_out_2_ms_bit,
       sign_bit_out_3_ms_bit;
  wire [3:0] xor_4_bit_1_result;

  sign_bit_out sign_bit_out_1 (.Input(A), .MS_bit(sign_bit_out_1_ms_bit));
  not not_1 (not_1_out, sign_bit_out_1_ms_bit);
  xor_4_bit xor_4_bit_1 (.Control(Sub), .B(B), .Result(xor_4_bit_1_result));
  sign_bit_out sign_bit_out_2 (.Input(xor_4_bit_1_result), .MS_bit(sign_bit_out_2_ms_bit));
  not not_2 (not_2_out, sign_bit_out_2_ms_bit);
  full_adder_4_bit full_adder_4_bit_1 (.A(A), .B(xor_4_bit_1_result), .Carry_in(Sub), .Carry(Carry), .Result(Result));
  sign_bit_out sign_bit_out_3 (.Input(Result), .MS_bit(sign_bit_out_3_ms_bit));
  not not_3 (not_3_out, sign_bit_out_3_ms_bit);
  and and_1 (and_1_out, not_3_out, sign_bit_out_2_ms_bit, sign_bit_out_1_ms_bit);
  and and_2 (and_2_out, sign_bit_out_3_ms_bit, not_2_out, not_1_out);
  or or_1 (Overflow, and_1_out, and_2_out);

  // Notes on the sheet:
  //   A31
  //   B31
  //   Result 31
endmodule

// 31th
module sign_bit_out (
  input  [3:0] Input,
  output MS_bit
);


  assign MS_bit = Input[3];
endmodule

// Reduce-OR
module reduce_or_4_bit (
  input  [3:0] Input,
  output Output
);

  or or_1 (Output, Input[0], Input[1], Input[2], Input[3]);
endmodule

// 4 bit ALU
module ALU_4_bit (
  input  Control0,
  input  Control1,
  input  [3:0] A,
  input  [3:0] B,
  output [3:0] Result,
  output Zero,
  output Negative,
  output Overflow,
  output Carry
);

  wire reduce_or_4_bit_1_output;
  wire [3:0] add_sub_1_result, and_4_bit_1_result, multiplexer_1_out, or_4_bit_1_result;

  and_4_bit and_4_bit_1 (.A(A), .B(B), .Result(and_4_bit_1_result));
  OR_4_bit or_4_bit_1 (.A(A), .B(B), .Result(or_4_bit_1_result));
  Add_sub add_sub_1 (.A(A), .B(B), .Sub(Control0), .Overflow(Overflow), .Carry(Carry), .Result(add_sub_1_result));
  Multiplexer #(.disabled("Z"), .width(4)) multiplexer_1 (
    .in0(and_4_bit_1_result), .in1(or_4_bit_1_result), .out(multiplexer_1_out), .sel(Control0));
  Multiplexer #(.disabled("Z"), .width(4)) multiplexer_2 (
    .in0(multiplexer_1_out), .in1(add_sub_1_result), .out(Result), .sel(Control1));
  sign_bit_out sign_bit_out_1 (.Input(Result), .MS_bit(Negative));
  reduce_or_4_bit reduce_or_4_bit_1 (.Input(Result), .Output(reduce_or_4_bit_1_output));
  not not_1 (Zero, reduce_or_4_bit_1_output);
endmodule

// Control \nUnit
module Controller (
  input  Clk,
  input  Reset,
  input  Q0,
  input  Qm1,
  input  [2:0] Count,
  output Cl_A_Qm1,
  output LOad_M_Q_Cnt,
  output Load_A,
  output C0,
  output C1,
  output Shr,
  output Dec_Cnt
);

  wire and_1_out, and_4_out, and_5_out, multiplexer_1_out, not_1_out, not_2_out, not_3_out, not_4_out,
       not_5_out, not_6_out, not_7_out, or_2_out;
  wire [1:0] rom_1_data;
  wire [2:0] and_2_out, and_3_out, bit_extender_1_out, bit_extender_2_out, bit_extender_3_out, CAR_q,
       or_1_out, rom_1_data_2;

  assign bit_extender_1_out = {{2{and_1_out}}, and_1_out};  // Bit_Extender bit_extender_1
  and and_1 (and_1_out, not_2_out, Qm1);
  not not_1 (not_1_out, and_1_out);
  assign bit_extender_2_out = {{2{not_1_out}}, not_1_out};  // Bit_Extender bit_extender_2
  assign and_2_out = 3'b100 & bit_extender_3_out & bit_extender_1_out;  // AND_Gate and_2, 3 bits wide
  assign or_1_out = and_2_out | rom_1_data_2 | and_3_out;  // OR_Gate or_1, 3 bits wide
  not not_2 (not_2_out, Q0);
  assign and_3_out = bit_extender_2_out & bit_extender_3_out & 3'b101;  // AND_Gate and_3, 3 bits wide
  assign bit_extender_3_out = {{2{and_4_out}}, and_4_out};  // Bit_Extender bit_extender_3
  and and_4 (and_4_out, not_3_out, CAR_q[1], not_4_out);
  not not_3 (not_3_out, CAR_q[2]);
  not not_4 (not_4_out, CAR_q[0]);
  ROM #(.addrWidth(3), .dataWidth(12)) rom_1 (
    .addr(CAR_q), .data({Cl_A_Qm1, LOad_M_Q_Cnt, Load_A, C0, C1, Shr, Dec_Cnt, rom_1_data_2, rom_1_data}));
  Counter #(.max('h7), .width(3)) CAR (
    .load(not_5_out), .D(or_1_out), .count(multiplexer_1_out), .Q(CAR_q), .clk(Clk), .clr(Reset));  // open: carry, up
  not not_5 (not_5_out, multiplexer_1_out);
  Multiplexer #(.disabled("Z"), .select(2)) multiplexer_1 (
    .in0(1'b0), .in1(1'b1), .in2(and_5_out), .in3(not_7_out), .out(multiplexer_1_out), .sel(rom_1_data));
  and and_5 (and_5_out, not_6_out, Q0);
  not not_6 (not_6_out, Qm1);
  not not_7 (not_7_out, or_2_out);
  or or_2 (or_2_out, Count[0], Count[1], Count[2]);

  // Notes on the sheet:
  //   Q0'Q-1
  //   contents of rom_1 (hex, n*v repeats v):
  //   1 c01 2 394 281 61 b 1c
  //   To choose only
  //   state 2 (010)
  //   Control Word Format: Clear (A, Q-1), Load (M, Q, Cnt), Load A, C0, C1, Shr, Dec Cnt, Address bits (3 bit), Selection bits (2 bit)
  //   Q0Q-1'
endmodule

module circuit_1 (
);

  Counter counter_1 ();  // open: load, D, count, Q, carry, up, clk, clr
endmodule
