// Logisim project 8-bit-ALU.circ as structural Verilog: 9 circuits, main circuit main
module main (
  input  Control0,
  input  Control1,
  input  [7:0] A,
  input  [7:0] B,
  output [7:0] Result,
  output Zero,
  output Negative,
  output Overflow,
  output Carry
);

  wire reduce_or_8_bit_1_output;
  wire [7:0] add_sub_1_result, and_8_bit_1_result, multiplexer_1_out, or_8_bit_1_result;

  and_8_bit and_8_bit_1 (.A(A), .B(B), .Result(and_8_bit_1_result));
  OR_8_bit or_8_bit_1 (.A(A), .B(B), .Result(or_8_bit_1_result));
  Add_sub add_sub_1 (.A(A), .B(B), .Sub(Control0), .Overflow(Overflow), .Carry(Carry), .Result(add_sub_1_result));
  Multiplexer #(.disabled("Z"), .width(8)) multiplexer_1 (
    .in0(and_8_bit_1_result), .in1(or_8_bit_1_result), .out(multiplexer_1_out), .sel(Control0));
  Multiplexer #(.disabled("Z"), .width(8)) multiplexer_2 (
    .in0(multiplexer_1_out), .in1(add_sub_1_result), .out(Result), .sel(Control1));
  bit_7_out bit_7_out_1 (.Input(Result), .bit_7(Negative));
  reduce_or_8_bit reduce_or_8_bit_1 (.Input(Result), .Output(reduce_or_8_bit_1_output));
  not not_1 (Zero, reduce_or_8_bit_1_output);
endmodule

// 8-bit AND
module and_8_bit (
  input  [7:0] A,
  input  [7:0] B,
  output [7:0] Result
);

  assign Result = A & B;  // AND_Gate and_1, 8 bits wide
endmodule

// 8-bit OR
module OR_8_bit (
  input  [7:0] A,
  input  [7:0] B,
  output [7:0] Result
);

  assign Result = A | B;  // OR_Gate or_1, 8 bits wide
endmodule

module Full_adder (
  input  Carry_in,
  input  A,
  input  B,
  output Result,
  output Carry_out
);

  wire and_1_out, and_2_out, xor_1_out;

  and and_1 (and_1_out, B, A);
  xor xor_1 (xor_1_out, A, B);
  or or_1 (Carry_out, and_1_out, and_2_out);
  and and_2 (and_2_out, xor_1_out, Carry_in);
  xor xor_2 (Result, Carry_in, xor_1_out);
endmodule

module full_adder_8_bit (
  input  Carry_in,
  input  [7:0] A,
  input  [7:0] B,
  output [7:0] Result,
  output Carry
);

  wire full_adder_1_carry_out, full_adder_2_carry_out, full_adder_3_carry_out, full_adder_4_carry_out,
       full_adder_5_carry_out, full_adder_6_carry_out, full_adder_7_carry_out;

  Full_adder full_adder_1 (
    .A(A[0]), .B(B[0]), .Carry_in(Carry_in), .Carry_out(full_adder_1_carry_out), .Result(Result[0]));
  Full_adder full_adder_2 (
    .A(A[1]), .B(B[1]), .Carry_in(full_adder_1_carry_out), .Carry_out(full_adder_2_carry_out),
    .Result(Result[1]));
  Full_adder full_adder_3 (
    .A(A[2]), .B(B[2]), .Carry_in(full_adder_2_carry_out), .Carry_out(full_adder_3_carry_out),
    .Result(Result[2]));
  Full_adder full_adder_4 (
    .A(A[3]), .B(B[3]), .Carry_in(full_adder_3_carry_out), .Carry_out(full_adder_4_carry_out),
    .Result(Result[3]));
  Full_adder full_adder_5 (
    .A(A[4]), .B(B[4]), .Carry_in(full_adder_4_carry_out), .Carry_out(full_adder_5_carry_out),
    .Result(Result[4]));
  Full_adder full_adder_6 (
    .A(A[5]), .B(B[5]), .Carry_in(full_adder_5_carry_out), .Carry_out(full_adder_6_carry_out),
    .Result(Result[5]));
  Full_adder full_adder_7 (
    .A(A[6]), .B(B[6]), .Carry_in(full_adder_6_carry_out), .Carry_out(full_adder_7_carry_out),
    .Result(Result[6]));
  Full_adder full_adder_8 (
    .A(A[7]), .B(B[7]), .Carry_in(full_adder_7_carry_out), .Carry_out(Carry), .Result(Result[7]));
endmodule

module xor_8_bit (
  input  Control,
  input  [7:0] B,
  output [7:0] Result
);

  wire [7:0] bit_extender_1_out;

  assign bit_extender_1_out = {{7{Control}}, Control};  // Bit_Extender bit_extender_1
  assign Result = bit_extender_1_out ^ B;  // XOR_Gate xor_1, 8 bits wide
endmodule

// 8-bit \nADD/SUB
module Add_sub (
  input  Sub,
  input  [7:0] A,
  input  [7:0] B,
  output [7:0] Result,
  output Carry,
  output Overflow
);

  wire and_1_out, and_2_out, bit_7_out_1_bit_7, bit_7_out_2_bit_7, bit_7_out_3_bit_7, not_1_out, not_2_out,
       not_3_out;
  wire [7:0] xor_8_bit_1_result;

  bit_7_out bit_7_out_1 (.Input(A), .bit_7(bit_7_out_1_bit_7));
  not not_1 (not_1_out, bit_7_out_1_bit_7);
  xor_8_bit xor_8_bit_1 (.Control(Sub), .B(B), .Result(xor_8_bit_1_result));
  bit_7_out bit_7_out_2 (.Input(xor_8_bit_1_result), .bit_7(bit_7_out_2_bit_7));
  not not_2 (not_2_out, bit_7_out_2_bit_7);
  full_adder_8_bit full_adder_8_bit_1 (.B(xor_8_bit_1_result), .A(A), .Carry_in(Sub), .Carry(Carry), .Result(Result));
  bit_7_out bit_7_out_3 (.Input(Result), .bit_7(bit_7_out_3_bit_7));
  not not_3 (not_3_out, bit_7_out_3_bit_7);
  and and_1 (and_1_out, not_3_out, bit_7_out_2_bit_7, bit_7_out_1_bit_7);
  and and_2 (and_2_out, bit_7_out_3_bit_7, not_2_out, not_1_out);
  or or_1 (Overflow, and_1_out, and_2_out);

  // Notes on the sheet:
  //   A31
  //   B31
  //   Result 31
endmodule

// 7th
module bit_7_out (
  input  [7:0] Input,
  output bit_7
);


  assign bit_7 = Input[7];
endmodule

// Reduce-OR
module reduce_or_8_bit (
  input  [7:0] Input,
  output Output
);

  or or_1 (Output, Input[0], Input[1], Input[2], Input[3], Input[5], Input[6], Input[7], Input[4]);
endmodule
