// Logisim project 8-bit-ALU.circ as structural Verilog: 9 circuits, main circuit main
module main (
  input  Control0,
  input  Control1,
  input  [7:0] A,
  input  [7:0] B,
  output [7:0] Result,
  output Zero,
  output Negative,
  output Overflow,
  output Carry
);

  wire n8_bit_reduce_or_1_output;
  wire [7:0] add_sub_1_result, multiplexer_1_out, n8_bit_and_1_result, n8_bit_or_1_result;

  _8_bit_and u_8_bit_and_1 (.A(A), .B(B), .Result(n8_bit_and_1_result));
  _8_bit_OR u_8_bit_or_1 (.A(A), .B(B), .Result(n8_bit_or_1_result));
  Add_sub add_sub_1 (.Sub(Control0), .A(A), .B(B), .Result(add_sub_1_result), .Carry(Carry), .Overflow(Overflow));
  Multiplexer #(.width(8), .enable("false")) multiplexer_1 (
    .in0(n8_bit_and_1_result), .in1(n8_bit_or_1_result), .out(multiplexer_1_out), .sel(Control0));
  Multiplexer #(.width(8), .enable("false")) multiplexer_2 (
    .in0(multiplexer_1_out), .in1(add_sub_1_result), .out(Result), .sel(Control1));
  _7th_bit_out u_7th_bit_out_1 (.Input(Result), ._7th_bit(Negative));
  _8_bit_reduce_or u_8_bit_reduce_or_1 (.Input(Result), .Output(n8_bit_reduce_or_1_output));
  not not_1 (Zero, n8_bit_reduce_or_1_output);
endmodule

// 8-bit AND
module _8_bit_and (
  input  [7:0] A,
  input  [7:0] B,
  output [7:0] Result
);

  assign Result = A & B;  // AND_Gate and_1, 8 bits wide
endmodule

// 8-bit OR
module _8_bit_OR (
  input  [7:0] A,
  input  [7:0] B,
  output [7:0] Result
);

  assign Result = A | B;  // OR_Gate or_1, 8 bits wide
endmodule

module Full_adder (
  input  Carry_in,
  input  A,
  input  B,
  output Result,
  output Carry_out
);

  wire and_1_out, and_2_out, xor_1_out;

  and and_1 (and_1_out, B, A);
  xor xor_1 (xor_1_out, A, B);
  or or_1 (Carry_out, and_1_out, and_2_out);
  and and_2 (and_2_out, xor_1_out, Carry_in);
  xor xor_2 (Result, Carry_in, xor_1_out);
endmodule

module _8_bit_full_adder (
  input  Carry_in,
  input  [7:0] A,
  input  [7:0] B,
  output [7:0] Result,
  output Carry
);

  wire full_adder_1_carry_out, full_adder_2_carry_out, full_adder_3_carry_out, full_adder_4_carry_out,
       full_adder_5_carry_out, full_adder_6_carry_out, full_adder_7_carry_out;

  Full_adder full_adder_1 (
    .Carry_in(Carry_in), .A(A[0]), .B(B[0]), .Result(Result[0]), .Carry_out(full_adder_1_carry_out));
  Full_adder full_adder_2 (
    .Carry_in(full_adder_1_carry_out), .A(A[1]), .B(B[1]), .Result(Result[1]),
    .Carry_out(full_adder_2_carry_out));
  Full_adder full_adder_3 (
    .Carry_in(full_adder_2_carry_out), .A(A[2]), .B(B[2]), .Result(Result[2]),
    .Carry_out(full_adder_3_carry_out));
  Full_adder full_adder_4 (
    .Carry_in(full_adder_3_carry_out), .A(A[3]), .B(B[3]), .Result(Result[3]),
    .Carry_out(full_adder_4_carry_out));
  Full_adder full_adder_5 (
    .Carry_in(full_adder_4_carry_out), .A(A[4]), .B(B[4]), .Result(Result[4]),
    .Carry_out(full_adder_5_carry_out));
  Full_adder full_adder_6 (
    .Carry_in(full_adder_5_carry_out), .A(A[5]), .B(B[5]), .Result(Result[5]),
    .Carry_out(full_adder_6_carry_out));
  Full_adder full_adder_7 (
    .Carry_in(full_adder_6_carry_out), .A(A[6]), .B(B[6]), .Result(Result[6]),
    .Carry_out(full_adder_7_carry_out));
  Full_adder full_adder_8 (
    .Carry_in(full_adder_7_carry_out), .A(A[7]), .B(B[7]), .Result(Result[7]), .Carry_out(Carry));
endmodule

module _8_bit_xor (
  input  Control,
  input  [7:0] B,
  output [7:0] Result
);

  wire [7:0] bit_extender_1_out;

  assign bit_extender_1_out = {{7{Control}}, Control};  // Bit_Extender bit_extender_1
  assign Result = bit_extender_1_out ^ B;  // XOR_Gate xor_1, 8 bits wide
endmodule

// 8-bit \nADD/SUB
module Add_sub (
  input  Sub,
  input  [7:0] A,
  input  [7:0] B,
  output [7:0] Result,
  output Carry,
  output Overflow
);

  wire and_1_out, and_2_out, n7th_bit_out_1__7th_bit, n7th_bit_out_2__7th_bit, n7th_bit_out_3__7th_bit,
       not_1_out, not_2_out, not_3_out;
  wire [7:0] n8_bit_xor_1_result;

  _7th_bit_out u_7th_bit_out_1 (.Input(A), ._7th_bit(n7th_bit_out_1__7th_bit));
  not not_1 (not_1_out, n7th_bit_out_1__7th_bit);
  _8_bit_xor u_8_bit_xor_1 (.B(B), .Result(n8_bit_xor_1_result), .Control(Sub));
  _7th_bit_out u_7th_bit_out_2 (.Input(n8_bit_xor_1_result), ._7th_bit(n7th_bit_out_2__7th_bit));
  not not_2 (not_2_out, n7th_bit_out_2__7th_bit);
  _8_bit_full_adder u_8_bit_full_adder_1 (
    .A(A), .B(n8_bit_xor_1_result), .Result(Result), .Carry_in(Sub), .Carry(Carry));
  _7th_bit_out u_7th_bit_out_3 (.Input(Result), ._7th_bit(n7th_bit_out_3__7th_bit));
  not not_3 (not_3_out, n7th_bit_out_3__7th_bit);
  and and_1 (and_1_out, not_3_out, n7th_bit_out_2__7th_bit, n7th_bit_out_1__7th_bit);
  and and_2 (and_2_out, n7th_bit_out_3__7th_bit, not_2_out, not_1_out);
  or or_1 (Overflow, and_1_out, and_2_out);

  // Notes on the sheet:
  //   A31
  //   B31
  //   Result 31
endmodule

// 7th
module _7th_bit_out (
  input  [7:0] Input,
  output _7th_bit
);


  assign _7th_bit = Input[7];
endmodule

// Reduce-OR
module _8_bit_reduce_or (
  input  [7:0] Input,
  output Output
);

  or or_1 (Output, Input[0], Input[1], Input[2], Input[3], Input[5], Input[6], Input[7], Input[4]);
endmodule
